// Logisim project control-logic.circ as structural Verilog: 1 circuit, main circuit control_logic
module control_logic (
  input  [31:0] Instruction,
  input  BrEq,
  input  BrLt,
  output PCSel,
  output RegWEn,
  output [2:0] ImmSel,
  output BrUn,
  output ASel,
  output BSel,
  output [3:0] ALUSel,
  output MemWEn,
  output [1:0] WBSel
);

  wire and_2_out, and_3_out, and_6_out, and_7_out, and_8_out, and_9_out, and_10_out, and_11_out, Btype,
       comparator_1_eq, comparator_2_eq, comparator_3_eq, comparator_4_eq, comparator_5_eq, comparator_6_eq,
       comparator_7_eq, comparator_8_eq, comparator_9_eq, comparator_10_eq, comparator_11_eq,
       comparator_12_eq, comparator_13_eq, compS, Itype, Jtype, not_3_out, not_4_out, not_5_out, op13, op33,
       op63, or_2_out, Stype, Utype;
  wire [2:0] and_12_out, and_13_out, and_14_out, and_15_out, and_16_out, bit_extender_2_out,
       bit_extender_3_out, bit_extender_4_out, bit_extender_5_out, bit_extender_6_out;
  wire [3:0] bit_extender_1_out, multiplexer_1_out, multiplexer_2_out, xor_1_out;
  wire [3:3] and_1_out;
  wire [15:0] rom_1_data;

  and and_1 (and_1_out[3], Instruction[25], op33);
  ROM #(.addrWidth(6), .dataWidth(16)) rom_1 (.data(rom_1_data));  // open: addr
  Comparator #(.mode("unsigned"), .width(7)) comparator_1 (
    .a(Instruction[6:0]), .b(7'b0000011), .eq(comparator_1_eq));  // open: gt, lt
  buf buffer_1 (WBSel[0], comparator_1_eq);
  Comparator #(.mode("unsigned"), .width(7)) comparator_2 (
    .a(Instruction[6:0]), .b(7'b0100011), .eq(comparator_2_eq));  // open: gt, lt
  buf buffer_2 (MemWEn, comparator_2_eq);
  Comparator #(.mode("unsigned"), .width(7)) comparator_3 (
    .a(Instruction[31:25]), .b(7'b0100000), .eq(comparator_3_eq));  // open: gt, lt
  Comparator #(.mode("unsigned"), .width(3)) comparator_4 (
    .a(Instruction[14:12]), .b(3'b000), .eq(comparator_4_eq));  // open: gt, lt
  Comparator #(.mode("unsigned"), .width(7)) comparator_5 (
    .a(Instruction[6:0]), .b(7'b0110011), .eq(comparator_5_eq));  // open: gt, lt
  buf buffer_3 (op13, comparator_6_eq);
  Comparator #(.mode("unsigned"), .width(7)) comparator_6 (
    .a(Instruction[6:0]), .b(7'b0010011), .eq(comparator_6_eq));  // open: gt, lt
  buf buffer_4 (op63, comparator_7_eq);
  Comparator #(.mode("unsigned"), .width(7)) comparator_7 (
    .a(Instruction[6:0]), .b(7'b1100011), .eq(comparator_7_eq));  // open: gt, lt
  assign bit_extender_1_out = {{3{Btype}}, Btype};  // Bit_Extender bit_extender_1
  Multiplexer #(.width(4)) multiplexer_1 (.in0(4'b1101), .in1(4'b1100), .out(multiplexer_1_out), .sel(and_2_out));
  and and_2 (and_2_out, comparator_3_eq, comparator_4_eq);
  buf buffer_5 (RegWEn, comparator_5_eq);
  not not_1 (BSel, comparator_5_eq);
  buf buffer_6 (op33, comparator_5_eq);
  buf buffer_7 (RegWEn, comparator_6_eq);
  assign xor_1_out = bit_extender_1_out ^ 4'b1111;  // XOR_Gate xor_1, 4 bits wide
  Multiplexer #(.width(4)) multiplexer_2 (
    .in0({and_1_out[3], Instruction[14:12]}), .in1(multiplexer_1_out), .out(multiplexer_2_out),
    .sel(and_3_out));
  and and_3 (and_3_out, and_2_out, op33);
  not not_2 (ASel, Btype);
  assign ALUSel = xor_1_out & multiplexer_2_out;  // AND_Gate and_4, 4 bits wide
  and and_5 (PCSel, compS, Btype);
  buf buffer_8 (RegWEn, MemWEn);
  or or_1 (Itype, op13, WBSel[0]);
  buf buffer_9 (Stype, MemWEn);
  buf buffer_10 (Btype, op63);
  buf buffer_11 (Utype, 1'b0);
  buf buffer_12 (Jtype, 1'b0);
  Comparator #(.mode("unsigned"), .width(3)) comparator_8 (
    .a(Instruction[14:12]), .b(3'b000), .eq(comparator_8_eq));  // open: gt, lt
  Comparator #(.mode("unsigned"), .width(3)) comparator_9 (
    .a(Instruction[14:12]), .b(3'b101), .eq(comparator_9_eq));  // open: gt, lt
  not not_3 (not_3_out, BrLt);
  Comparator #(.mode("unsigned"), .width(3)) comparator_10 (
    .a(Instruction[14:12]), .b(3'b001), .eq(comparator_10_eq));  // open: gt, lt
  not not_4 (not_4_out, BrEq);
  Comparator #(.mode("unsigned"), .width(3)) comparator_11 (
    .a(Instruction[14:12]), .b(3'b111), .eq(comparator_11_eq));  // open: gt, lt
  not not_5 (not_5_out, BrLt);
  Comparator #(.mode("unsigned"), .width(3)) comparator_12 (
    .a(Instruction[14:12]), .b(3'b110), .eq(comparator_12_eq));  // open: gt, lt
  Comparator #(.mode("unsigned"), .width(3)) comparator_13 (
    .a(Instruction[14:12]), .b(3'b100), .eq(comparator_13_eq));  // open: gt, lt
  and and_6 (and_6_out, comparator_8_eq, BrEq);
  and and_7 (and_7_out, comparator_9_eq, or_2_out);
  or or_2 (or_2_out, BrEq, not_3_out);
  and and_8 (and_8_out, comparator_10_eq, not_4_out);
  and and_9 (and_9_out, comparator_11_eq, not_5_out);
  and and_10 (and_10_out, comparator_12_eq, BrLt);
  and and_11 (and_11_out, comparator_13_eq, BrLt);
  or or_3 (BrUn, comparator_11_eq, comparator_12_eq);
  assign bit_extender_2_out = {{2{Itype}}, Itype};  // Bit_Extender bit_extender_2
  assign bit_extender_3_out = {{2{Stype}}, Stype};  // Bit_Extender bit_extender_3
  assign bit_extender_4_out = {{2{Btype}}, Btype};  // Bit_Extender bit_extender_4
  assign bit_extender_5_out = {{2{Utype}}, Utype};  // Bit_Extender bit_extender_5
  assign bit_extender_6_out = {{2{Jtype}}, Jtype};  // Bit_Extender bit_extender_6
  assign and_12_out = 3'b000 & bit_extender_2_out;  // AND_Gate and_12, 3 bits wide
  assign and_13_out = 3'b001 & bit_extender_3_out;  // AND_Gate and_13, 3 bits wide
  assign and_14_out = 3'b010 & bit_extender_4_out;  // AND_Gate and_14, 3 bits wide
  assign and_15_out = 3'b011 & bit_extender_5_out;  // AND_Gate and_15, 3 bits wide
  assign and_16_out = 3'b100 & bit_extender_6_out;  // AND_Gate and_16, 3 bits wide
  or or_4 (compS, and_6_out, and_7_out, and_8_out, and_9_out, and_10_out, and_11_out);
  assign ImmSel = and_12_out | and_13_out | and_14_out | and_15_out | and_16_out;  // OR_Gate or_5, 3 bits wide

  assign WBSel[1] = 1'b0;

  // Other names for the same wires on the sheet: func3[2:0] = Instruction[14:12]; op23 = MemWEn; op03 = WBSel[0];
  //   OpCode[6:0] = Instruction[6:0]; func7[6:0] = Instruction[31:25]

  // Notes on the sheet:
  //   INPUTS to your circuit
  //   Connect ROM Input here ->
  //   ROM FOR CONTROL LOGIC
  //   DON'T CHANGE THE LOCATIONS OF THE INPUTS AND OUTPUTS!
  //   This is only if you choose to do the ROM option
  //   CONNECT
  //   WIRE
  //   TO
  //   USE
  //   ROM
  //   OUTPUT from your circuit
  //   Reminder: If using ROM, use combinational logic for PCSel
endmodule
