// Logisim project cpu.circ as structural Verilog: 1 circuit, main circuit cpu
module cpu (
  input  clk,
  input  [31:0] Instruction,
  input  [31:0] MemReadData,
  output [31:0] MemAddress,
  output [31:0] ProgramCounter,
  output [31:0] ra,
  output [31:0] sp,
  output [31:0] t0,
  output [31:0] t1,
  output [31:0] t2,
  output [31:0] s0,
  output [31:0] s1,
  output [31:0] a0,
  output [3:0] MemWriteMask,
  output [31:0] MemWriteData
);

  wire ASel, branch_comp_1_breq, branch_comp_1_brlt, BrUn, BSel, control_logic_1_memwen, PCSel, RegWEn;
  wire [1:0] control_logic_1_wbsel;
  wire [2:0] ImmSel;
  wire [3:0] control_logic_1_alusel;
  wire [31:0] adder_1_out, buffer_1_out, imm_gen_1_immediate, Instruction_t, multiplexer_1_out,
       multiplexer_2_out, multiplexer_3_out, multiplexer_4_out, multiplexer_5_out, partial_load_1_datatoreg,
       regfile_1_readdata1, regfile_1_readdata2, register_2_q, register_3_q;

  Adder #(.width(32)) adder_1 (.a(buffer_1_out), .b(32'h4), .out(adder_1_out));  // open: cin, cout
  Multiplexer #(.width(32)) multiplexer_1 (.in0(adder_1_out), .in1(MemAddress), .out(multiplexer_1_out), .sel(PCSel));
  Register #(.width(32)) PC (.D(multiplexer_1_out), .clk(clk), .Q(ProgramCounter));  // open: en, clr
  Multiplexer #(.width(32)) multiplexer_2 (.in0(Instruction), .in1(32'h13), .out(multiplexer_2_out), .sel(PCSel));
  assign buffer_1_out = ProgramCounter;  // Buffer buffer_1, 32 bits wide
  Register #(.width(32)) register_1 (.D(multiplexer_2_out), .clk(clk), .Q(Instruction_t));  // open: en, clr
  Register #(.width(32)) register_2 (.D(buffer_1_out), .clk(clk), .Q(register_2_q));  // open: en, clr
  Register #(.width(32)) register_3 (.D(adder_1_out), .clk(clk), .Q(register_3_q));  // open: en, clr
  regfile regfile_1 (
    .ReadIndex1(Instruction_t[19:15]), .ReadIndex2(Instruction_t[24:20]), .WriteIndex(Instruction_t[11:7]),
    .WriteData(multiplexer_5_out), .RegWEn(RegWEn), .clk(clk), .ra(ra), .sp(sp), .t0(t0), .t1(t1), .t2(t2),
    .s0(s0), .s1(s1), .a0(a0), .ReadData1(regfile_1_readdata1), .ReadData2(regfile_1_readdata2));
  imm_gen imm_gen_1 (.Instruction(Instruction_t), .ImmSel(ImmSel), .Immediate(imm_gen_1_immediate));
  Multiplexer #(.width(32)) multiplexer_3 (
    .in0(regfile_1_readdata2), .in1(imm_gen_1_immediate), .out(multiplexer_3_out), .sel(BSel));
  control_logic control_logic_1 (
    .Instruction(Instruction_t), .BrEq(branch_comp_1_breq), .BrLt(branch_comp_1_brlt), .PCSel(PCSel),
    .RegWEn(RegWEn), .ImmSel(ImmSel), .BrUn(BrUn), .ASel(ASel), .BSel(BSel), .ALUSel(control_logic_1_alusel),
    .MemWEn(control_logic_1_memwen), .WBSel(control_logic_1_wbsel));
  Multiplexer #(.width(32)) multiplexer_4 (
    .in0(register_2_q), .in1(regfile_1_readdata1), .out(multiplexer_4_out), .sel(ASel));
  alu alu_1 (.A(multiplexer_4_out), .B(multiplexer_3_out), .ALUSel(control_logic_1_alusel), .ALUResult(MemAddress));
  branch_comp branch_comp_1 (
    .BrData1(regfile_1_readdata1), .BrData2(regfile_1_readdata2), .BrUn(BrUn), .BrEq(branch_comp_1_breq),
    .BrLt(branch_comp_1_brlt));
  Multiplexer #(.select(2), .width(32)) multiplexer_5 (
    .in0(MemAddress), .in1(partial_load_1_datatoreg), .in2(register_3_q), .in3(imm_gen_1_immediate),
    .out(multiplexer_5_out), .sel(control_logic_1_wbsel));
  partial_load partial_load_1 (
    .Instruction(Instruction_t), .MemAddress(MemAddress), .DataFromMem(MemReadData),
    .DataToReg(partial_load_1_datatoreg));
  partial_store partial_store_1 (
    .Instruction(Instruction_t), .MemAddress(MemAddress), .DataFromReg(regfile_1_readdata2),
    .MemWEn(control_logic_1_memwen), .MemWriteMask(MemWriteMask), .DataToMem(MemWriteData));

  // Other names for the same wires on the sheet: Instruction_o[31:0] = Instruction; rd[4:0] = Instruction_t[11:7];
  //   rs1[4:0] = Instruction_t[19:15]; rs2[4:0] = Instruction_t[24:20]

  // Notes on the sheet:
  //   To IMEM
  //   IMEM (do **NOT** move this)
  //   From IMEM
  //   Inputs/Outputs for testing. Do **NOT** move these.
  //   To DMEM
  //   DMEM (do **NOT** move this)
  //   From DMEM
endmodule
